// Logisim project yurova_var1.circ as structural Verilog: 2 circuits, main circuit main
module main (
  input  \_4бит ,
  input  \_3_бит ,
  input  \_2_бит ,
  input  \_1_бит ,
  input  \_0_бит ,
  output out_6,
  output out_7,
  output out_8,
  output \Есть_согласная 
);

  wire and_1_out, and_2_out, and_3_out, and_4_out, and_5_out, and_6_out, and_7_out, and_8_out, and_9_out,
       and_10_out, and_11_out, not_1_out, not_2_out, not_3_out, not_4_out, not_5_out, not_6_out, not_7_out;

  not not_1 (not_1_out, \_2_бит );
  not not_2 (not_2_out, \_4бит );
  not not_3 (not_3_out, \_4бит );
  not not_4 (not_4_out, \_3_бит );
  not not_5 (not_5_out, \_2_бит );
  not not_6 (not_6_out, \_1_бит );
  not not_7 (not_7_out, \_0_бит );
  and and_1 (and_1_out, not_3_out, not_4_out, \_2_бит );
  and and_2 (and_2_out, not_3_out, \_3_бит );
  and and_3 (and_3_out, not_3_out, not_4_out, not_1_out, \_1_бит );
  or or_1 (out_7, and_1_out, and_2_out);
  or or_2 (out_8, and_2_out, and_3_out);
  and and_4 (and_4_out, not_4_out, not_5_out, \_1_бит );
  and and_5 (and_5_out, not_4_out, \_2_бит , not_7_out);
  and and_6 (and_6_out, \_3_бит , not_5_out, not_7_out);
  and and_7 (and_7_out, not_3_out, \_3_бит , \_2_бит , not_6_out);
  and and_8 (and_8_out, \_4бит , not_4_out, not_5_out, not_6_out);
  and and_9 (and_9_out, not_4_out, \_2_бит , \_1_бит , \_0_бит );
  and and_10 (and_10_out, not_3_out, \_3_бит , not_5_out, \_1_бит , \_0_бит );
  and and_11 (and_11_out, not_2_out, \_3_бит , \_2_бит , \_1_бит , not_7_out);
  or or_3 (\Есть_согласная , and_4_out, and_5_out, and_6_out, and_7_out, and_8_out, and_9_out, and_10_out, and_11_out);

  assign out_6 = \_4бит ;

  // Notes on the sheet:
  //   Вариант 1
  //   Номер самого старшего бита
endmodule

module _1_variant (
  input  [3:0] \Число ,
  input  [3:0] in_2,
  output out_3,
  output [3:0] out_4
);

  wire xnor_1_out, xnor_2_out;

  Divider #(.width(4)) divider_1 (.a(\Число ), .b(in_2), .rem(out_4));  // open: out, upper
  xnor xnor_1 (xnor_1_out, \Число [0], \Число [3]);
  xnor xnor_2 (xnor_2_out, \Число [1], \Число [2]);
  and and_1 (out_3, xnor_1_out, xnor_2_out);

  // Notes on the sheet:
  //   Вариант 10
  //   Делим на 11
  //   Остаток от деления
  //   Если симметрично, то 1
endmodule
