// Logisim project yurova_lab4.circ as structural Verilog: 1 circuit, main circuit main
module main (
  input  R,
  input  S,
  input  S_2,
  input  R_2,
  input  S_3,
  input  C,
  input  R_3,
  input  S_4,
  input  R_4,
  input  S_5,
  input  R_5,
  input  S_6,
  input  R_6,
  output out_14,
  output out_15,
  output out_16,
  output out_17,
  output out_18,
  output out_19,
  output out_20,
  output out_21,
  output out_22,
  output out_23,
  output out_24,
  output out_25
);

  wire nand_1_out, nand_2_out, nand_3_out, nand_4_out, nand_5_out, nand_6_out, nand_9_out, nand_10_out,
       nand_17_out, nand_18_out;

  nand nand_1 (nand_1_out, S_4, S_4);
  nand nand_2 (nand_2_out, nand_1_out, R_4);
  nand nand_3 (nand_3_out, S_5, nand_4_out);
  nand nand_4 (nand_4_out, R_5, R_5);
  nand nand_5 (nand_5_out, S_6, S_6);
  nand nand_6 (nand_6_out, R_6, R_6);
  nor nor_1 (out_14, R, out_15);
  nor nor_2 (out_15, out_14, S);
  nand nand_7 (out_16, S_2, out_17);
  nand nand_8 (out_17, out_16, R_2);
  nand nand_9 (nand_9_out, S_3, C);
  nand nand_10 (nand_10_out, C, R_3);
  nand nand_11 (out_18, nand_9_out, out_19);
  nand nand_12 (out_19, out_18, nand_10_out);
  nand nand_13 (out_20, nand_1_out, out_21);
  nand nand_14 (out_21, out_20, nand_2_out);
  nand nand_15 (out_22, nand_3_out, out_23);
  nand nand_16 (out_23, out_22, nand_4_out);
  nand nand_17 (nand_17_out, S_6, nand_6_out);
  nand nand_18 (nand_18_out, nand_5_out, R_6);
  nand nand_19 (out_24, nand_17_out, out_25);
  nand nand_20 (out_25, out_24, nand_18_out);

  // Notes on the sheet:
  //   S-триггер
  //   R-триггер
  //   E-триггер
  //   Синхронный RS триггер
  //   Асинхронный RS триггер с прямыми входами
  //   Асинхронный  RS триггер с инверсивными входами
endmodule
