// Logisim project yurova_lab5.circ as structural Verilog: 3 circuits, main circuit D-триггер
module \D_триггер  (
  input  D,
  input  C,
  output out_3,
  output out_4
);

  wire nand_1_out, nand_2_out;

  nand nand_1 (nand_1_out, D, C);
  nand nand_2 (nand_2_out, nand_1_out, C);
  nand nand_3 (out_3, nand_1_out, out_4);
  nand nand_4 (out_4, out_3, nand_2_out);
endmodule

module \T_триггер  (
  input  in_1,
  input  T,
  input  C,
  output out_4,
  output out_5
);

  wire nand_1_out, nand_2_out, nand_3_out;

  nand nand_1 (nand_1_out, T, C);
  nand nand_2 (nand_2_out, in_1, nand_1_out);
  nand nand_3 (nand_3_out, nand_2_out, nand_1_out);
  nand nand_4 (out_4, nand_2_out, out_5);
  nand nand_5 (out_5, out_4, nand_3_out);
endmodule

module \JK_триггер  (
  input  J,
  input  C,
  input  K,
  output out_4,
  output out_5
);

  wire nand_1_out, nand_2_out, nand_3_out, nand_4_out, nand_5_out, nand_6_out;

  nand nand_1 (nand_1_out, out_5, J, C);
  nand nand_2 (nand_2_out, C, K, out_4);
  nand nand_3 (nand_3_out, nand_1_out, nand_4_out);
  nand nand_4 (nand_4_out, nand_3_out, nand_2_out);
  nand nand_5 (nand_5_out, nand_1_out, nand_3_out);
  nand nand_6 (nand_6_out, nand_4_out, nand_2_out);
  nand nand_7 (out_4, nand_5_out, out_5);
  nand nand_8 (out_5, out_4, nand_6_out);
endmodule
