// Logisim project lab6.circ as structural Verilog: 6 circuits, main circuit Схема сравнения
module \Схема_сравнения  (
  input  in_1,
  input  in_2,
  output out_3
);

  wire and_1_out, and_2_out, not_1_out, not_2_out;

  not not_1 (not_1_out, in_1);
  not not_2 (not_2_out, in_2);
  and and_1 (and_1_out, not_1_out, in_2);
  and and_2 (and_2_out, in_1, not_2_out);
  or or_1 (out_3, and_1_out, and_2_out);
endmodule

module \Полусумматор  (
  input  in_1,
  input  in_2,
  output out_3,
  output out_4
);

  \Схема_сравнения  \u_схема_сравнения_1  (.in_1(in_1), .in_2(in_2), .out_3(out_4));
  and and_1 (out_3, in_2, in_2);
endmodule

module \Полный_сумматор  (
  input  in_1,
  input  in_2,
  input  in_3,
  output out_4,
  output out_5
);

  wire \полусумматор_1_out_3 , \полусумматор_1_out_4 , \полусумматор_2_out_3 ;

  \Полусумматор  \u_полусумматор_1  (
    .in_1(in_1), .in_2(in_2), .out_3(\полусумматор_1_out_3 ), .out_4(\полусумматор_1_out_4 ));
  \Полусумматор  \u_полусумматор_2  (
    .in_1(\полусумматор_1_out_4 ), .in_2(in_3), .out_3(\полусумматор_2_out_3 ), .out_4(out_5));
  or or_1 (out_4, \полусумматор_1_out_3 , \полусумматор_2_out_3 );
endmodule

module \_4_сумматора  (
  input  in_1,
  input  in_2,
  input  in_3,
  input  in_4,
  input  in_5,
  input  in_6,
  input  in_7,
  input  in_8,
  input  in_9,
  output out_10,
  output out_11,
  output out_12,
  output out_13,
  output out_14
);

  wire \полный_сумматор_1_out_4 , \полный_сумматор_2_out_4 , \полный_сумматор_3_out_4 ;

  \Полный_сумматор  \u_полный_сумматор_1  (
    .in_1(in_7), .in_2(in_7), .in_3(in_7), .out_4(\полный_сумматор_1_out_4 ), .out_5(out_14));
  \Полный_сумматор  \u_полный_сумматор_2  (
    .in_1(in_5), .in_2(in_6), .in_3(\полный_сумматор_1_out_4 ), .out_4(\полный_сумматор_2_out_4 ),
    .out_5(out_13));
  \Полный_сумматор  \u_полный_сумматор_3  (
    .in_1(in_3), .in_2(in_4), .in_3(\полный_сумматор_2_out_4 ), .out_4(\полный_сумматор_3_out_4 ),
    .out_5(out_12));
  \Полный_сумматор  \u_полный_сумматор_4  (
    .in_1(in_1), .in_2(in_2), .in_3(\полный_сумматор_3_out_4 ), .out_4(out_10), .out_5(out_11));

  assign in_8 = in_7;
  assign in_9 = in_7;
endmodule

module \Полусумматор_теор  (
  input  in_1,
  input  in_2,
  output out_3,
  output out_4
);

  wire not_1_out, or_1_out;

  or or_1 (or_1_out, in_1, in_2);
  and and_1 (out_4, in_1, in_2);
  not not_1 (not_1_out, out_4);
  and and_2 (out_3, or_1_out, not_1_out);
endmodule

module \Сумматор_теор  (
  input  in_1,
  input  in_2,
  input  in_3,
  output out_4,
  output out_5
);

  wire and_1_out, and_2_out, and_3_out, and_4_out, and_5_out, not_1_out, or_1_out;

  and and_1 (and_1_out, in_1, in_2);
  and and_2 (and_2_out, in_1, in_3);
  and and_3 (and_3_out, in_2, in_3);
  or or_1 (or_1_out, in_1, in_2, in_3);
  and and_4 (and_4_out, in_1, in_2, in_3);
  or or_2 (out_4, and_1_out, and_2_out, and_3_out);
  not not_1 (not_1_out, out_4);
  and and_5 (and_5_out, not_1_out, or_1_out);
  or or_3 (out_5, and_5_out, and_4_out);
endmodule
